# Fritzing sketch DomusGuard (saved by Fritzing 0.9.2b)
circuit board: 8.46667cm x 5.64444cm
breadboards: 2

parts:
  Raspberry_Pi1 = Raspberry Pi 2
  Arduino_NRF = Arduino Pro Mini v13
  J4 = shrouded pin header, 8 pins [form="♂ (shrouded male)"]
  NRF = NRF24L01
  J3 = double row female pin header, 8 pins [form="♀ (female)"]
  12_V_Alarm = Power plug  # not connected
  Rx1 = mystery part, 4 pins [chip_label=?]
  Arduino_433 = Arduino Pro Mini v13
  Q1 = PNP-Transistor [package="TO92 [THT]"]  # not connected

nets:
  N1: Raspberry_Pi1.3v3, J3.pin2
  N2: Raspberry_Pi1.GPIO2, J3.pin3
  N3: Raspberry_Pi1.GPIO3, J3.pin4
  N4: Raspberry_Pi1.GND, J3.pin1
  N5: Raspberry_Pi1.5V, J3.pin8
  5V: Arduino_NRF.VCC, J4.pin8
  GND: Arduino_NRF.GND, J4.pin1, NRF.GND, Arduino_433.GND
  N6: Arduino_NRF.A4, J4.pin3
  N7: Arduino_NRF.A5, J4.pin4
  N8: Arduino_NRF.D13/SCK, NRF.SCK
  N9: Arduino_NRF.D12/MISO, NRF.MISO
  N10: Arduino_NRF.D11_PWM/MOSI, NRF.MOSI
  N11: Arduino_NRF.D10_PWM/SS, NRF.CSN
  N12: Arduino_NRF.D8, NRF.CE
  N13: Arduino_NRF.D2, NRF.IRQ
  3.3V: J4.pin2, NRF.VCC
  N14: Rx1.pin1, Arduino_433.VCC
  N15: Rx1.pin3, Arduino_433.D11_PWM/MOSI
